// Logisim project Aula 2 Circuitos Lógicos.circ as structural Verilog: 3 circuits, main circuit main
module main (
  input  [3:0] in_1,
  input  [3:0] in_2,
  output out_3,
  output [3:0] out_4
);

  // Probe on in_1
  // Probe on out_4
  ADD4 add4_1 (.out_3(out_3), .A(in_1), .B(in_2), .out_4(out_4));
  // Probe on in_2
endmodule

module ADD_1 (
  input  A,
  input  B,
  input  C,
  output out_4,
  output out_5
);

  wire and_1_out, and_2_out, and_3_out, and_4_out, and_5_out, and_6_out, and_7_out;

  and and_1 (and_1_out, ~A, ~B, C);  // AND_Gate
  and and_2 (and_2_out, ~A, B, ~C);  // AND_Gate
  and and_3 (and_3_out, A, ~B, ~C);  // AND_Gate
  and and_4 (and_4_out, A, B, C);
  and and_5 (and_5_out, ~A, B, C);  // AND_Gate
  and and_6 (and_6_out, A, ~B, C);  // AND_Gate
  and and_7 (and_7_out, A, B, ~C);  // AND_Gate
  or or_1 (out_4, and_1_out, and_2_out, and_3_out, and_4_out);
  or or_2 (out_5, and_4_out, and_5_out, and_6_out, and_7_out);
endmodule

module ADD4 (
  input  [3:0] A,
  input  [3:0] B,
  output out_3,
  output [3:0] out_4
);

  wire add_1_2_out_5, add_1_3_out_5, add_1_4_out_5;

  // Probe on A
  ADD_1 add_1_1 (.out_4(out_4[3]), .out_5(out_3), .A(A[3]), .B(B[3]), .C(add_1_2_out_5));
  ADD_1 add_1_2 (.out_4(out_4[2]), .out_5(add_1_2_out_5), .A(A[2]), .B(B[2]), .C(add_1_3_out_5));
  // Probe on out_4
  ADD_1 add_1_3 (.out_4(out_4[1]), .out_5(add_1_3_out_5), .A(A[1]), .B(B[1]), .C(add_1_4_out_5));
  ADD_1 add_1_4 (.out_4(out_4[0]), .out_5(add_1_4_out_5), .A(A[0]), .B(B[0]), .C(1'b0));
  // Probe on B
endmodule
